# Fritzing sketch hygrometer-plant-chapter03 (saved by Fritzing 0.9.5d)
breadboards: 1

parts:
  Composant1 = Arduino Uno (Rev3)
  R1 = Resistor [tolerance=±5% resistance=220 package=THT]
  LED1 = LED - 5mm [color="Red (633nm)" package="5 mm [THT]"]  # not connected
  Composant2 = Soil Moisture Sensor

nets:
  N1: Composant1.A0, Composant2.VCC
  GND: Composant1.GND, R1.Pin_1, Composant2.GND
  N2: Composant1.5V, Composant2.SIG
