# Fritzing sketch hygrometer-plant-chapter04 (saved by Fritzing 0.9.5d)
breadboards: 1

parts:
  Composant1 = Arduino Uno (Rev3)
  R1 = Resistor [tolerance=±5% resistance=220 package=THT]
  LED1 = LED - 5mm [color="Red (633nm)" package="5 mm [THT]"]  # not connected
  Composant2 = Soil Moisture Sensor
  R2 = Resistor [tolerance=±5% resistance=220 package=THT]
  LED2 = LED - 5mm [color="Yellow (595nm)" package="5 mm [THT]"]
  R3 = Resistor [tolerance=±5% resistance=220 package=THT]
  LED3 = LED - 5mm [color="Green (570nm)" package="5 mm [THT]"]

nets:
  N1: Composant1.A0, Composant2.VCC
  N2: Composant1.D10_PWM/SS, LED2.cathode
  N3: Composant1.D11_PWM/MOSI, LED3.cathode
  GND: Composant1.GND, R1.Pin_1, Composant2.GND, R2.Pin_1, R3.Pin_1
  N4: Composant1.5V, Composant2.SIG
  N5: R2.Pin_0, LED2.anode
  N6: R3.Pin_0, LED3.anode
